# Fritzing sketch Fritzing Circuit (saved by Fritzing 0.9.3b)
circuit board: 8.46667cm x 5.64444cm
breadboards: 1

parts:
  Q2 = Basic FET N-Channel [package="D2Pak [SMD]"]
  R2 = Resistor [tolerance=±5% resistance=10k package="0805 [SMD]"]
  R1 = Resistor [tolerance=±5% resistance=10k package="0805 [SMD]"]
  A1 = RGB Strip LED
  R3 = Resistor [tolerance=±5% resistance=10k package="0805 [SMD]"]
  Q5 = Basic FET N-Channel [package="D2Pak [SMD]"]
  Q6 = Basic FET N-Channel [package="D2Pak [SMD]"]
  J1 = Power Jack [package=power_jack_combo]
  esp1 = ESP32 DevKitc V4  # not connected

nets (from the breadboard view):
  N1: Q2.Gate, R1.Pin_1
  N2: Q2.drain, A1.Common_Connect, A1.Blue_Connect, A1.Red_Connect, A1.Green_Connect, Q5.drain, Q6.drain, J1.PWR
  N3: Q2.source, R2.Pin_0, R1.Pin_0, R3.Pin_0, Q5.source, Q6.source, J1.GND
  N4: R2.Pin_1, Q6.Gate
  N5: R3.Pin_1, Q5.Gate

custom parts:
  RGB Strip LED: A tri-color Strip LED with red, green and blue. Pin order: red - common cathode - blue - green
  ESP32 DevKitc V4: ESP32-DevKitC board with ESP32-WROOM-32 module. ESP32-DevKitC V4 is a small-sized ESP32-based development board produced by Espressif. Most of the pins on the ESP module are broken out to the pin headers on the board. The pins D0, D1, D2, D3, CMD and CLK are used internally for communication between ESP32 and SPI flash memory. They are grouped on both sides near the USB connector. Avoid using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

// code stored in the sketch: UnoLEDBasic.ino

//12v LED strip
#define green 6
#define red 5
#define blue 3

///////SOUND SENSOR/////////////////
#define BUTTON_PIN 2



void setup()
{

  
    pinMode(BUTTON_PIN, INPUT_PULLUP);
    pinMode(LED_BUILTIN, OUTPUT);
    
    Serial.begin (9600);

    analogWrite(blue, 255);
    analogWrite(green, 255);
    analogWrite(red, 255);
    digitalWrite(LED_BUILTIN, HIGH);
    delay(500);
  
    analogWrite(blue, 0);
    analogWrite(green, 0);
    analogWrite(red, 0);
    digitalWrite(LED_BUILTIN, LOW);
    delay(500);

    analogWrite(blue, 255);
    analogWrite(green, 255);
    analogWrite(red, 255);
    digitalWrite(LED_BUILTIN, HIGH);
    delay(500);

    analogWrite(blue, 0);
    analogWrite(green, 0);
    analogWrite(red, 0);
    digitalWrite(LED_BUILTIN, LOW);
    delay(500);

    analogWrite(blue, 255);
    analogWrite(green, 255);
    analogWrite(red, 255);
    digitalWrite(LED_BUILTIN, HIGH);
    delay(500);

    analogWrite(blue, 0);
    analogWrite(green, 0);
    analogWrite(red, 0);
    digitalWrite(LED_BUILTIN, LOW);
    delay(500);
}

void loop(){
	
for (int i=o; i<255; i++){
	analogWrite(blue, i);
  analogWrite(green, i);
  analogWrite(red, i);
  digitalWrite(LED_BUILTIN, HIGH);
	delay(500);
}

for (int j=255; j>0; i--){
	analogWrite(blue, j);
  analogWrite(green, j);
  analogWrite(red, j);
  digitalWrite(LED_BUILTIN, Low);
	delay(500);
}

 
}//end of loop/////////////////////////////////////////////////////////////
